# Fritzing sketch Arduino_with_Bluetooth (saved by Fritzing 0.9.2b)
breadboards: 1

parts:
  Arduino_UNO = Arduino Uno (Rev3)
  Bluetooth_HC-06_Module = Bluetooth HC-06

nets:
  N1: Arduino_UNO.D0/RX, Bluetooth_HC-06_Module.TXD
  N2: Arduino_UNO.D1/TX, Arduino_UNO.D2, Bluetooth_HC-06_Module.RXD
  5V: Arduino_UNO.5V, Bluetooth_HC-06_Module.VCC
  GND: Arduino_UNO.GND, Bluetooth_HC-06_Module.GND
