# Fritzing sketch Arduino_With_buzzer (saved by Fritzing 0.9.2b)
breadboards: 1

parts:
  Buzzer = Piezo Speaker
  Arduino_UNO = Arduino Uno (Rev3)

nets:
  N1: Buzzer.pin1, Arduino_UNO.GND
  N2: Buzzer.pin2, Arduino_UNO.D2
