# Fritzing sketch Arduino_with_HBridge_v1 (saved by Fritzing 0.9.2b)
breadboards: 1

parts:
  Arduino_UNO = Arduino Uno (Rev3)
  S1 = H-Bridge with L298N
  Motor_1 = DC Motor
  Motor_2 = DC Motor

nets:
  N1: Arduino_UNO.D9_PWM, S1.IN4
  N2: Arduino_UNO.D3_PWM, S1.IN1
  N3: Arduino_UNO.D5_PWM, S1.IN2
  N4: Arduino_UNO.D6_PWM, S1.IN3
  5V: Arduino_UNO.5V, S1.5V
  GND: Arduino_UNO.GND, S1.GND
  N5: S1.ENA, S1.ENA-5V
  N6: S1.ENB, S1.ENB-5V
  N7: S1.M1-01, Motor_2.pin_1
  N8: S1.M1-02, Motor_2.pin_2
  N9: S1.M2-01, Motor_1.pin_2
  N10: S1.M2-02, Motor_1.pin_1

custom parts:
  H-Bridge with L298N: h-bridge
