# Fritzing sketch Arduino_with_HBridge_v2 (saved by Fritzing 0.9.2b)
breadboards: 1

parts:
  Arduino_UNO = Arduino Uno (Rev3)
  S1 = H-Bridge with L298N
  Motor_1 = DC Motor
  Motor_2 = DC Motor
  S3 = H-Bridge with L298N
  Motor_1_2 = DC Motor
  Motor_2_2 = DC Motor
  Bateria = Battery block 9V

nets:
  N1: Arduino_UNO.D8, S3.IN3
  N2: Arduino_UNO.D9_PWM, S1.IN4
  N3: Arduino_UNO.D13/SCK, S3.IN4
  N4: Arduino_UNO.D3_PWM, S1.IN1
  N5: Arduino_UNO.D4, S3.IN1
  N6: Arduino_UNO.D5_PWM, S1.IN2
  N7: Arduino_UNO.D6_PWM, S1.IN3
  N8: Arduino_UNO.D7, S3.IN2
  5V: Arduino_UNO.5V, S1.5V, S3.5V
  GND: Arduino_UNO.GND, S1.GND, S3.GND, Bateria.-
  12V: Arduino_UNO.VIN, S1.12V, S3.12V, Bateria.+
  N9: S1.ENA, S1.ENA-5V
  N10: S1.ENB, S1.ENB-5V
  N11: S1.M1-01, Motor_2.pin_1
  N12: S1.M1-02, Motor_2.pin_2
  N13: S1.M2-01, Motor_1.pin_2
  N14: S1.M2-02, Motor_1.pin_1
  N15: S3.ENA, S3.ENA-5V
  N16: S3.ENB, S3.M2-02, S3.ENB-5V, Motor_1_2.pin_1
  N17: S3.M1-01, Motor_2_2.pin_1
  N18: S3.M1-02, Motor_2_2.pin_2
  N19: S3.M2-01, Motor_1_2.pin_2

custom parts:
  H-Bridge with L298N: h-bridge
