# Fritzing sketch Arduino_with_LDR (saved by Fritzing 0.9.2b)
breadboards: 1

parts:
  Arduino_UNO = Arduino Uno (Rev3)
  Light_Dependent_Resistor = Photocell (LDR) [package=THT]
  Resistência = Resistor [tolerance=±5% resistance=220 package=THT]

nets:
  N1: Arduino_UNO.A1, Light_Dependent_Resistor.pin_0, Resistência.Pin_1
  N2: Arduino_UNO.5V, Light_Dependent_Resistor.pin_1
  N3: Arduino_UNO.GND, Resistência.Pin_0
