# Fritzing sketch Arduino_with_LED (saved by Fritzing 0.9.2b)

parts:
  Arduino_UNO = Arduino Uno (Rev3)
  LED = LED - 5mm [color="Red (633nm)" package="5 mm [THT]"]

nets:
  N1: Arduino_UNO.D10_PWM/SS, LED.anode
  N2: Arduino_UNO.GND, LED.cathode
