# Fritzing sketch Arduino_with_TemperatureLM35 (saved by Fritzing 0.9.2b)
breadboards: 1

parts:
  Arduino_UNO = Arduino Uno (Rev3)
  T1 = LM35 Temperature Sensor [package="TO92 [THT]"]

nets:
  N1: Arduino_UNO.A0, T1.Vout
  GND: Arduino_UNO.GND, T1.GND
  N2: Arduino_UNO.5V, T1.+Vs
