# Fritzing sketch Arduino_and_HC-SR04 (saved by Fritzing 0.9.2b)
breadboards: 1

parts:
  Arduino_UNO = Arduino Uno (Rev3)
  Sensor_Ultrasons_HC-SR04 = SRF05 Ultrasonic Rangefinder

nets:
  N1: Arduino_UNO.D11_PWM/MOSI, Sensor_Ultrasons_HC-SR04.Echo
  N2: Arduino_UNO.D12/MISO, Sensor_Ultrasons_HC-SR04.Trig
  GND: Arduino_UNO.GND, Sensor_Ultrasons_HC-SR04.GND
  5V: Arduino_UNO.5V, Sensor_Ultrasons_HC-SR04.VCC
